// Digital circuit bcu.dig as structural Verilog
module bcu (
  input  A,
  input  B,
  input  [1:0] BROp,
  input  PCsel,
  output O
);

  wire comparator_1_lt, comparator_2_eq, comparator_3_eq, comparator_3_gt, multiplexer_1_out, or_1_out;

  Comparator comparator_1 (.a(A), .b(B), .lt(comparator_1_lt));  // open: gt, eq
  Comparator comparator_2 (.a(A), .b(B), .eq(comparator_2_eq));  // open: gt, lt
  Comparator comparator_3 (.a(A), .b(B), .gt(comparator_3_gt), .eq(comparator_3_eq));  // open: lt
  or or_1 (or_1_out, comparator_3_gt, comparator_3_eq);
  Multiplexer #(.Selector_Bits(2)) multiplexer_1 (
    .sel(BROp), .in_0(1'b0), .in_1(comparator_1_lt), .in_2(comparator_2_eq), .in_3(or_1_out),
    .out(multiplexer_1_out));
  or or_2 (O, PCsel, multiplexer_1_out);

  // Notes on the sheet:
  //   blt
  //   beq
  //   bge
endmodule
